# Fritzing sketch breadboard_wiring (saved by Fritzing 0.9.3b)
breadboards: 1

parts:
  Part1 = Arduino Uno (Rev3)
  GY1 = MPU-6050 Board GY-521 [form="♀ (female)" package=THT]
  8x8_LED_Modul_mit_MAX1 = 8x8 LED Modul mit MAX7219 [package=THT]

nets:
  N1: Part1.D8, 8x8_LED_Modul_mit_MAX1.DIN_Eingang
  N2: Part1.D10_PWM/SS, 8x8_LED_Modul_mit_MAX1.CS_Eingang
  N3: Part1.D13/SCK, 8x8_LED_Modul_mit_MAX1.CLK_Eingang
  N4: Part1.GND, GY1.pin2, 8x8_LED_Modul_mit_MAX1.GND_Eingang
  N5: Part1.A4/SDA, GY1.pin4
  N6: Part1.A5/SCL, GY1.pin3
  N7: Part1.D2, GY1.pin8
  N8: Part1.3V3, GY1.pin1
  N9: Part1.5V, 8x8_LED_Modul_mit_MAX1.VCC_Eingang

custom parts:
  MPU-6050 Board GY-521: Acelerometro y Giroscopio MPU-6050 Board GY-521
